# Fritzing sketch hawkingclock (saved by Fritzing 0.9.3b)

parts:
  Onderdeel1 = Arduino Uno (Rev3)
  ZS-042_RTC1 = ZS-042 RTC Module

nets:
  N1: Onderdeel1.A4/SDA, ZS-042_RTC1.SDA
  N2: Onderdeel1.A5/SCL, ZS-042_RTC1.SCL
  5V: Onderdeel1.5V, ZS-042_RTC1.VCC
  GND: Onderdeel1.GND, ZS-042_RTC1.GND
